# Fritzing sketch lcd (saved by Fritzing 0.9.3b)
breadboards: 1

parts:
  Raspberry_Pi_1 = Raspberry Pi 3 [part_number=RPI-3-V1.2]
  LCD1 = LCD screen

nets:
  N1: Raspberry_Pi_1.GIPO21, LCD1.RS
  N2: Raspberry_Pi_1.GIPO20, LCD1.R/W
  N3: Raspberry_Pi_1.GIPO16, LCD1.E
  N4: Raspberry_Pi_1.GIPO7, LCD1.DB0
  N5: Raspberry_Pi_1.GIPO8, LCD1.DB1
  N6: Raspberry_Pi_1.GIPO25, LCD1.DB2
  N7: Raspberry_Pi_1.GIPO24, LCD1.DB3
  N8: Raspberry_Pi_1.GIPO23, LCD1.DB4
  N9: Raspberry_Pi_1.GIPO18, LCD1.DB5
  N10: Raspberry_Pi_1.GIPO15, LCD1.DB6
  N11: Raspberry_Pi_1.GIPO14, LCD1.DB7
  GND: Raspberry_Pi_1.GND, LCD1.VSS, LCD1.V0, LCD1.LED-
  5V: Raspberry_Pi_1.5V, LCD1.VDD, LCD1.LED+
